# Fritzing sketch Schematic (saved by Fritzing 0.9.3b)
breadboards: 1

parts:
  U1 = ESP32-38PinWide [part_number=ESP32-38PinWide]
  Part1 = Adafruit DRV8833 DC/Stepper Motor Driver [part_number="Adafruit #3297"]
  M1 = DC Motor
  U2 = Battery Holders [package=lipo-1100mAh]
  C1 = Capacitor [package=cap-pth-small2]
  U3 = V_REG_LD1117VXX [package=78xxl]
  J1 = Basic Servo

nets:
  N1: U1.GPIO13, J1.pulse
  N2: U1.GPIO11, U2.-, C1.1, U3.OUT, J1.gnd
  N3: U1.GPIO18, Part1.AIN1
  N4: U1.GPIO19, Part1.AIN2
  N5: Part1.AOUT2, M1.pin_1
  N6: Part1.AOUT1, M1.pin_2
  N7: U2.+, C1.2, U3.GND
  N8: U3.IN, J1.vcc

custom parts:
  ESP32-38PinWide: Generic 38-Pin ESP32 with wide format (only access to one side of pins on a breadboard) based on Stephen Lilley's HiLetgo ESP-WROOM-32 ESP32 ESP-32S Development Board.
  Adafruit DRV8833 DC/Stepper Motor Driver: Spin two DC motors or step one bi-polar or uni-polar stepper with up to 1.2A per channel using the DRV8833. This motor driver chip is a nice alternative to the TB6612 driver. Like that chip, you get 2 full H-bridges, but this chip is better for low voltage uses (can run from 2.7V up to 10.8V motor power) and has built in current limiting capability. We set it up for 1A current limiting so you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
